# Fritzing sketch hudsonriver-monitor (saved by Fritzing 0.9.3b)
breadboards: 1

parts:
  U1_-_XBee = XBEE-1 [package=xbee-1_lock]
  U2 = LIPO-2000mAh [package=lipo-2000]
  U2_2 = TMP36 [package=to-92-kit]
  IC1 = Voltage Regulator [package=to-92]
  C1 = Ceramic Capacitor [capacitance=1µF package="100 mil [THT, multilayer]"]
  C3 = Ceramic Capacitor [capacitance=1µF package="100 mil [THT, multilayer]"]
  C2 = Ceramic Capacitor [capacitance=1µF package="100 mil [THT, multilayer]"]
  U3_-_GPS_Receiver = SUP500F [package=sup500f]

nets:
  N1: U1_-_XBee.VDD, IC1.OUT, C1.1
  N2: U1_-_XBee.DOUT, U3_-_GPS_Receiver.RX-I
  N3: U1_-_XBee.DIN, U3_-_GPS_Receiver.TX-O
  GND: U1_-_XBee.GND, U2.-, U2_2.GND, IC1.GND, C1.0, C3.0, C2.1, U3_-_GPS_Receiver.GND
  VCC: U1_-_XBee.DIO9, U2_2.VCC, C3.1, U3_-_GPS_Receiver.VCC, U3_-_GPS_Receiver.VBAT
  N4: U1_-_XBee.DIO1, U3_-_GPS_Receiver.PPS
  N5: U1_-_XBee.DIO0, U2_2.VOUT
  N6: U2.+, IC1.IN, C2.0
